# Fritzing sketch Arduino semaphore (saved by Fritzing 0.9.3b)
circuit board: 10.8937cm x 6.96145cm
breadboards: 1

parts:
  R1 = Resistor [tolerance=±5% resistance=220 package=THT]
  R3 = Resistor [tolerance=±5% resistance=220 package=THT]
  LED1 = LED - 5mm [color="Green (570nm)" package="5 mm [THT]"]
  LED2 = LED - 5mm [color="Yellow (595nm)" package="5 mm [THT]"]
  LED3 = LED - 5mm [color="Red (635nm)" package="5 mm [THT]"]
  Part1 = Arduino Uno (Rev3)
  R2 = Resistor [tolerance=±5% resistance=220 package=THT]

nets (from the schematic view):
  N1: R1.Pin_0, R3.Pin_0
  N2: R1.Pin_1, LED1.cathode
  N3: R3.Pin_1, LED3.cathode
  N4: LED1.anode, Part1.D8
  N5: LED2.cathode, R2.Pin_1
  N6: LED2.anode, Part1.D10_PWM/SS
  N7: LED3.anode, Part1.D12/MISO
  N8: Part1.GND, R2.Pin_0

// code stored in the sketch: semaphore.ino
#define GREEN_PIN 8
#define YELLOW_PIN 10
#define RED_PIN 12

int red_on = 3000;
int red_yellow_on = 1000;
int green_on = 3000;
int green_blink = 500;
int yellow_on = 1000;

void setup(){
    // set the ports as output to control LEDs
    pinMode(RED_PIN, OUTPUT);
    pinMode(YELLOW_PIN, OUTPUT);
    pinMode(GREEN_PIN, OUTPUT);
}

void loop(){
    // control the semaphore
    // turn on the RED_PIN
    digitalWrite(RED_PIN, HIGH);
    // wait while the red signal is on
    delay(red_on);

    // turn on the YELLOW_PIN
    digitalWrite(YELLOW_PIN, HIGH);
    delay(red_yellow_on);

    // turn on the YELLOW_PIN
    digitalWrite(RED_PIN, LOW);
    digitalWrite(YELLOW_PIN, LOW);
    digitalWrite(GREEN_PIN, HIGH);
    delay(green_on);
    digitalWrite(GREEN_PIN, LOW);

    for (int i=0; i<3; i=i+1){
        delay(green_blink);
        digitalWrite(GREEN_PIN, HIGH);
        delay(green_blink);
        digitalWrite(GREEN_PIN, LOW);
    }

    // turn yellow on now
    digitalWrite(YELLOW_PIN, HIGH);
    delay(yellow_on);
    digitalWrite(YELLOW_PIN, LOW);
    
}
